// Digital circuit Banc de regisre.dig as structural Verilog
module Banc_de_regisre (
  input  [4:0] RD,
  input  W_REG,
  input  [4:0] RS1,
  input  [4:0] RS2,
  input  [31:0] RES,
  output [31:0] src1,
  output [31:0] src2
);

  wire and_1_out, and_2_out, and_3_out, and_4_out, decoder_1_out_0, decoder_1_out_1, decoder_1_out_2,
       decoder_1_out_3, decoder_2_out_0, decoder_2_out_1, decoder_2_out_2, decoder_2_out_3, decoder_3_out_0,
       decoder_3_out_1, decoder_3_out_2, decoder_3_out_3;
  wire [31:0] mon_gros_banc_de_registre_1_src1, mon_gros_banc_de_registre_1_src2,
       mon_gros_banc_de_registre_2_src1, mon_gros_banc_de_registre_2_src2, mon_gros_banc_de_registre_3_src1,
       mon_gros_banc_de_registre_3_src2, mon_gros_banc_de_registre_4_src1, mon_gros_banc_de_registre_4_src2;

  Decoder #(.Selector_Bits(2)) decoder_1 (
    .sel(RD[4:3]), .out_0(decoder_1_out_0), .out_1(decoder_1_out_1), .out_2(decoder_1_out_2),
    .out_3(decoder_1_out_3));
  and and_1 (and_1_out, W_REG, decoder_1_out_0);
  and and_2 (and_2_out, W_REG, decoder_1_out_1);
  and and_3 (and_3_out, W_REG, decoder_1_out_2);
  and and_4 (and_4_out, W_REG, decoder_1_out_3);
  MON_GROS_BANC_DE_REGISTRE mon_gros_banc_de_registre_1 (
    .w(and_1_out), .\Entrée (RD[2:0]), .rs(RES), .RES1(RS1[2:0]), .RES2(RS2[2:0]),
    .src1(mon_gros_banc_de_registre_1_src1), .src2(mon_gros_banc_de_registre_1_src2));
  MON_GROS_BANC_DE_REGISTRE mon_gros_banc_de_registre_2 (
    .w(and_2_out), .\Entrée (RD[2:0]), .rs(RES), .RES1(RS1[2:0]), .RES2(RS2[2:0]),
    .src1(mon_gros_banc_de_registre_2_src1), .src2(mon_gros_banc_de_registre_2_src2));
  MON_GROS_BANC_DE_REGISTRE mon_gros_banc_de_registre_3 (
    .w(and_3_out), .\Entrée (RD[2:0]), .rs(RES), .RES1(RS1[2:0]), .RES2(RS2[2:0]),
    .src1(mon_gros_banc_de_registre_3_src1), .src2(mon_gros_banc_de_registre_3_src2));
  MON_GROS_BANC_DE_REGISTRE mon_gros_banc_de_registre_4 (
    .w(and_4_out), .\Entrée (RD[2:0]), .rs(RES), .RES1(RS1[2:0]), .RES2(RS2[2:0]),
    .src1(mon_gros_banc_de_registre_4_src1), .src2(mon_gros_banc_de_registre_4_src2));
  Decoder #(.Selector_Bits(2)) decoder_2 (
    .sel(RS1[4:3]), .out_0(decoder_2_out_0), .out_1(decoder_2_out_1), .out_2(decoder_2_out_2),
    .out_3(decoder_2_out_3));
  assign src1 = decoder_2_out_0 ? mon_gros_banc_de_registre_1_src1 : 32'bz;  // Driver driver_1
  assign src1 = decoder_2_out_1 ? mon_gros_banc_de_registre_2_src1 : 32'bz;  // Driver driver_2
  assign src1 = decoder_2_out_2 ? mon_gros_banc_de_registre_3_src1 : 32'bz;  // Driver driver_3
  assign src1 = decoder_2_out_3 ? mon_gros_banc_de_registre_4_src1 : 32'bz;  // Driver driver_4
  Decoder #(.Selector_Bits(2)) decoder_3 (
    .sel(RS2[4:3]), .out_0(decoder_3_out_0), .out_1(decoder_3_out_1), .out_2(decoder_3_out_2),
    .out_3(decoder_3_out_3));
  assign src2 = decoder_3_out_0 ? mon_gros_banc_de_registre_1_src2 : 32'bz;  // Driver driver_5
  assign src2 = decoder_3_out_1 ? mon_gros_banc_de_registre_2_src2 : 32'bz;  // Driver driver_6
  assign src2 = decoder_3_out_2 ? mon_gros_banc_de_registre_3_src2 : 32'bz;  // Driver driver_7
  assign src2 = decoder_3_out_3 ? mon_gros_banc_de_registre_4_src2 : 32'bz;  // Driver driver_8
endmodule
