// Digital circuit MON GROS BANC DE REGISTRE.dig as structural Verilog
module MON_GROS_BANC_DE_REGISTRE (
  input  w,
  input  [2:0] \Entrée ,
  input  [31:0] rs,
  input  [2:0] RES1,
  input  [2:0] RES2,
  output [31:0] src1,
  output [31:0] src2
);

  wire and_1_out, and_2_out, and_3_out, and_4_out, and_5_out, and_6_out, and_7_out, and_8_out,
       decoder_1_out_0, decoder_1_out_1, decoder_1_out_2, decoder_1_out_3, decoder_1_out_4, decoder_1_out_5,
       decoder_1_out_6, decoder_1_out_7, decoder_2_out_0, decoder_2_out_1, decoder_2_out_2, decoder_2_out_3,
       decoder_2_out_4, decoder_2_out_5, decoder_2_out_6, decoder_2_out_7, decoder_3_out_0, decoder_3_out_1,
       decoder_3_out_2, decoder_3_out_3, decoder_3_out_4, decoder_3_out_5, decoder_3_out_6, decoder_3_out_7;
  wire [31:0] a0_q, a1_q, a2_q, a3_q, a4_q, a5_q, a6_q, a7_q;

  Decoder #(.Selector_Bits(3)) decoder_1 (
    .sel(\Entrée ), .out_0(decoder_1_out_0), .out_1(decoder_1_out_1), .out_2(decoder_1_out_2),
    .out_3(decoder_1_out_3), .out_4(decoder_1_out_4), .out_5(decoder_1_out_5), .out_6(decoder_1_out_6),
    .out_7(decoder_1_out_7));
  and and_1 (and_1_out, w, decoder_1_out_0);
  and and_2 (and_2_out, w, decoder_1_out_1);
  and and_3 (and_3_out, w, decoder_1_out_2);
  and and_4 (and_4_out, w, decoder_1_out_3);
  and and_5 (and_5_out, w, decoder_1_out_4);
  and and_6 (and_6_out, w, decoder_1_out_5);
  and and_7 (and_7_out, w, decoder_1_out_6);
  and and_8 (and_8_out, w, decoder_1_out_7);
  D_FF #(.Bits(32)) a0 (.D(rs), .C(and_1_out), .Q(a0_q));  // open: nQ
  D_FF #(.Bits(32)) a1 (.D(rs), .C(and_2_out), .Q(a1_q));  // open: nQ
  D_FF #(.Bits(32)) a2 (.D(rs), .C(and_3_out), .Q(a2_q));  // open: nQ
  D_FF #(.Bits(32)) a3 (.D(rs), .C(and_4_out), .Q(a3_q));  // open: nQ
  D_FF #(.Bits(32)) a4 (.D(rs), .C(and_5_out), .Q(a4_q));  // open: nQ
  D_FF #(.Bits(32)) a5 (.D(rs), .C(and_6_out), .Q(a5_q));  // open: nQ
  D_FF #(.Bits(32)) a6 (.D(rs), .C(and_7_out), .Q(a6_q));  // open: nQ
  D_FF #(.Bits(32)) a7 (.D(rs), .C(and_8_out), .Q(a7_q));  // open: nQ
  assign src1 = decoder_2_out_0 ? a0_q : 32'bz;  // Driver driver_1
  assign src1 = decoder_2_out_1 ? a1_q : 32'bz;  // Driver driver_2
  assign src1 = decoder_2_out_2 ? a2_q : 32'bz;  // Driver driver_3
  assign src1 = decoder_2_out_3 ? a3_q : 32'bz;  // Driver driver_4
  assign src1 = decoder_2_out_4 ? a4_q : 32'bz;  // Driver driver_5
  assign src1 = decoder_2_out_5 ? a5_q : 32'bz;  // Driver driver_6
  assign src1 = decoder_2_out_6 ? a6_q : 32'bz;  // Driver driver_7
  assign src1 = decoder_2_out_7 ? a7_q : 32'bz;  // Driver driver_8
  Decoder #(.Selector_Bits(3)) decoder_2 (
    .sel(RES1), .out_0(decoder_2_out_0), .out_1(decoder_2_out_1), .out_2(decoder_2_out_2),
    .out_3(decoder_2_out_3), .out_4(decoder_2_out_4), .out_5(decoder_2_out_5), .out_6(decoder_2_out_6),
    .out_7(decoder_2_out_7));
  assign src2 = decoder_3_out_0 ? a0_q : 32'bz;  // Driver driver_9
  assign src2 = decoder_3_out_1 ? a1_q : 32'bz;  // Driver driver_10
  assign src2 = decoder_3_out_2 ? a2_q : 32'bz;  // Driver driver_11
  assign src2 = decoder_3_out_3 ? a3_q : 32'bz;  // Driver driver_12
  assign src2 = decoder_3_out_4 ? a4_q : 32'bz;  // Driver driver_13
  assign src2 = decoder_3_out_5 ? a5_q : 32'bz;  // Driver driver_14
  assign src2 = decoder_3_out_6 ? a6_q : 32'bz;  // Driver driver_15
  assign src2 = decoder_3_out_7 ? a7_q : 32'bz;  // Driver driver_16
  Decoder #(.Selector_Bits(3)) decoder_3 (
    .sel(RES2), .out_0(decoder_3_out_0), .out_1(decoder_3_out_1), .out_2(decoder_3_out_2),
    .out_3(decoder_3_out_3), .out_4(decoder_3_out_4), .out_5(decoder_3_out_5), .out_6(decoder_3_out_6),
    .out_7(decoder_3_out_7));
endmodule
