// Digital circuit Mon processeur avec tunnel et cc mini version4.dig as structural Verilog
module Mon_processeur_avec_tunnel_et_cc_mini_version4 (
  input  clk,
  output [31:0] out_2
);

  wire beq_1_p1, delay_1_out, delay_2_out, delay_3_out, delay_4_out, delay_5_out, delay_6_out, GATE_MDR,
       gate_pc, GATE_RS2, Jalr, multiplexer_6_out, MUX_MDR, MUX_sub, MUX_SW, MUX_UAL, not_1_out, not_2_out,
       OE, RES_GATE, W_MAR, W_MDR, W_PC, W_REG, W_RI, WE;
  wire [0:0] and_1_out;
  wire [3:0] RI_q_2;
  wire [6:0] UP_CODE;
  wire [7:0] MAR_q_2, RI_q, RI_q_3;
  wire [9:0] RI_q_5;
  wire [11:0] multiplexer_3_out;
  wire [20:11] RI_q_4;
  wire [31:0] add_1_s, banc_de_regisre_1_src1, banc_de_regisre_1_src2, beq_1_p4, bitextender_1_out,
       bitextender_2_out, bitextender_3_out, MAR_q, MDR_q, multiplexer_1_out, multiplexer_2_out,
       multiplexer_4_out, multiplexer_5_out, pc_q, ual_1_res;
  wire [31:7] driver_2_out;

  BitExtender #(.inputBits(13), .outputBits(32)) bitextender_1 (
    .in({RI_q_4[20], RI_q[7], RI_q_5[9:4], RI_q_2, 1'b0}), .out(bitextender_1_out));
  Multiplexer #(.Selector_Bits(2), .Bits(32)) multiplexer_1 (
    .sel({RI_q[2], and_1_out[0]}), .in_0(32'h4), .in_1(bitextender_1_out), .in_2(bitextender_2_out),
    .in_3({32{1'b0}}), .out(multiplexer_1_out));
  Add #(.Bits(32)) add_1 (.a(pc_q), .b(multiplexer_1_out), .c_i(1'b0), .s(add_1_s));  // open: c_o
  Multiplexer #(.Bits(32)) multiplexer_2 (.sel(Jalr), .in_0(add_1_s), .in_1(out_2), .out(multiplexer_2_out));
  Delay delay_1 (.in(W_PC), .out(delay_1_out));
  BitExtender #(.inputBits(21), .outputBits(32)) bitextender_2 (
    .in({RI_q_4[20], RI_q_3, RI_q_4[11], RI_q_5, 1'b0}), .out(bitextender_2_out));
  and and_1 (and_1_out[0], beq_1_p1, not_1_out);
  D_FF #(.Bits(32)) pc (.D(multiplexer_2_out), .C(delay_1_out), .Q(pc_q));  // open: nQ
  not not_1 (not_1_out, RI_q[2]);
  assign out_2 = gate_pc ? pc_q : 32'bz;  // Driver driver_1
  Delay delay_2 (.in(W_MAR), .out(delay_2_out));
  D_FF #(.Bits(32)) RI (
    .D(out_2), .C(delay_3_out), .Q({RI_q_4[20], RI_q_5, RI_q_4[11], RI_q_3, RI_q_2, RI_q}));  // open: nQ
  Delay #(.delayTime(2)) delay_3 (.in(W_RI), .out(delay_3_out));
  D_FF #(.Bits(32)) MAR (.D(out_2), .C(delay_2_out), .Q({MAR_q[31:10], MAR_q_2, MAR_q[1:0]}));  // open: nQ
  // BEQ beq_1: pin names not known; wires that end beside it: beq_1_p1, RI_q[6], {RI_q_3[2], RI_q_3[0]}, beq_1_p4
  circuit_controle circuit_controle_1 (
    .clock(clk), .OPCODE(UP_CODE), .GATE_PC(gate_pc), .W_MAR(W_MAR), .MUX_MDR(MUX_MDR), .W_MDR(W_MDR),
    .W_RI(W_RI), .GATE_MDR(GATE_MDR), .W_PC(W_PC), .GATE_RES(RES_GATE), .W_REG(W_REG), .MUX_S(MUX_SW),
    .MUX_SUB(MUX_sub), .MUX_UAL(MUX_UAL), .OE_RAM(OE), .WE_RAM(WE), .MUX_JALR(Jalr), .GATE_RS2(GATE_RS2));
  Multiplexer #(.Bits(12)) multiplexer_3 (
    .sel(MUX_SW), .in_0({RI_q_4[20], RI_q_5, RI_q_4[11]}), .in_1({RI_q_4[20], RI_q_5[9:4], RI_q_2, RI_q[7]}),
    .out(multiplexer_3_out));
  Delay delay_4 (.in(W_REG), .out(delay_4_out));
  BitExtender #(.inputBits(12), .outputBits(32)) bitextender_3 (.in(multiplexer_3_out), .out(bitextender_3_out));
  Multiplexer #(.Bits(32)) multiplexer_4 (
    .sel(MUX_MDR), .in_0(out_2), .in_1({driver_2_out, UP_CODE}), .out(multiplexer_4_out));
  D_FF #(.Bits(32)) MDR (.D(multiplexer_4_out), .C(delay_5_out), .Q(MDR_q));  // open: nQ
  Delay delay_5 (.in(W_MDR), .out(delay_5_out));
  assign {driver_2_out, UP_CODE} = OE ? MDR_q : 32'bz;  // Driver driver_2
  Banc_de_regisre banc_de_regisre_1 (
    .RD({RI_q_2, RI_q[7]}), .W_REG(delay_4_out), .RS1(RI_q_3[7:3]), .RS2({RI_q_5[3:0], RI_q_4[11]}),
    .RES(out_2), .src1(banc_de_regisre_1_src1), .src2(banc_de_regisre_1_src2));
  assign out_2 = GATE_MDR ? MDR_q : 32'bz;  // Driver driver_3
  Multiplexer #(.Bits(32)) multiplexer_5 (
    .sel(MUX_UAL), .in_0(banc_de_regisre_1_src2), .in_1(bitextender_3_out), .out(multiplexer_5_out));
  assign out_2 = GATE_RS2 ? banc_de_regisre_1_src2 : 32'bz;  // Driver driver_4
  Delay delay_6 (.in(WE), .out(delay_6_out));
  not not_2 (not_2_out, OE);
  assign beq_1_p4 = RI_q[6] ? ual_1_res : 32'bz;  // Driver driver_5
  Multiplexer multiplexer_6 (.sel(MUX_sub), .in_0(RI_q_5[9]), .in_1(1'b1), .out(multiplexer_6_out));
  RAMSinglePortSel #(.AddrBits(8), .Bits(32)) ramsingleportsel_1 (
    .A(MAR_q_2), .CS(1'b1), .WE(delay_6_out), .OE(not_2_out), .D({driver_2_out, UP_CODE}));
  UAL ual_1 (
    .src1(banc_de_regisre_1_src1), .src2(multiplexer_5_out), .sub(multiplexer_6_out), .fct_3(RI_q_3[2:0]),
    .res(ual_1_res));  // open: cout
  assign out_2 = RES_GATE ? ual_1_res : 32'bz;  // Driver driver_6
endmodule
