// Digital circuit UAL.dig as structural Verilog
module UAL (
  input  [31:0] src1,
  input  [31:0] src2,
  input  sub,
  input  [2:0] fct_3,
  output [31:0] res,
  output cout
);

  wire [31:0] add_1_s, and_1_out, bitextender_1_out, or_1_out, xor_1_out, xor_2_out;

  assign and_1_out = src1 & src2;  // And and_1, 32 bits wide
  assign or_1_out = src1 | src2;  // Or or_1, 32 bits wide
  assign xor_1_out = src1 ^ src2;  // XOr xor_1, 32 bits wide
  Multiplexer #(.Selector_Bits(3), .Bits(32)) multiplexer_1 (
    .sel(fct_3), .in_0(add_1_s), .in_1({32{1'b0}}), .in_2({32{1'b0}}), .in_3({32{1'b0}}), .in_4(xor_1_out),
    .in_5({32{1'b0}}), .in_6(or_1_out), .in_7(and_1_out), .out(res));
  BitExtender #(.inputBits(1), .outputBits(32)) bitextender_1 (.in(sub), .out(bitextender_1_out));
  assign xor_2_out = bitextender_1_out ^ src2;  // XOr xor_2, 32 bits wide
  Add #(.Bits(32)) add_1 (.a(src1), .b(xor_2_out), .c_i(sub), .s(add_1_s), .c_o(cout));
endmodule
